# Fritzing sketch ds18b20_reader (saved by Fritzing 0.9.3b)

parts:
  U2 = ESP8266 WiFi Module [part_number=ESP8266]
  R6 = Resistor [tolerance=±5% resistance=1k package=THT]
  R7 = Resistor [tolerance=±5% resistance=1k package=THT]

nets:
  N1: U2.IO2, R6.Pin_1
  N2: U2.3.3V, R6.Pin_0, R7.Pin_0
  N3: U2.GND, U2.IO15
  N4: U2.RST, U2.XPD
  N5: U2.CHIP_EN, R7.Pin_1
